# Fritzing sketch schematic (saved by Fritzing 0.9.9b)
breadboards: 1

parts:
  U1 = Photon
  K1 = songle relay [part_number=SRD-5VDC-SL-C]
  V1 = DC Power [voltage=12V part_number="Bench Power Supply"]  # not connected

nets:
  GND: U1.GND, K1.GND
  N1: U1.D1, K1.COMMON
  3V3: U1.3V3, K1.VCC
